// Logisim project control-logic.circ as structural Verilog: 1 circuit, main circuit control_logic
module control_logic (
  input  [31:0] Instruction,
  input  BrEq,
  input  BrLt,
  output PCSel,
  output RegWEn,
  output [2:0] ImmSel,
  output BrUn,
  output ASel,
  output BSel,
  output [3:0] ALUSel,
  output MemWEn,
  output [1:0] WBSel
);

  wire add, addi, and_10_out, and_11_out, and_12_out, and_13_out, and_14_out, and_15_out, and_r, andi, auipc,
       B_type, beq, bge, bgeu, blt, bltu, bne, comparator_1_eq, comparator_2_eq, comparator_3_eq,
       comparator_4_eq, comparator_10_eq, comparator_11_eq, comparator_12_eq, comparator_13_eq,
       comparator_14_eq, comparator_15_eq, comparator_16_eq, comparator_17_eq, comparator_18_eq,
       comparator_19_eq, comparator_20_eq, comparator_21_eq, comparator_22_eq, comparator_23_eq,
       comparator_24_eq, comparator_25_eq, comparator_26_eq, comparator_27_eq, comparator_28_eq,
       comparator_29_eq, comparator_30_eq, comparator_31_eq, comparator_32_eq, comparator_33_eq,
       comparator_34_eq, comparator_35_eq, comparator_36_eq, comparator_37_eq, comparator_38_eq,
       comparator_39_eq, comparator_40_eq, comparator_41_eq, comparator_42_eq, comparator_43_eq,
       comparator_44_eq, comparator_45_eq, comparator_46_eq, comparator_50_eq, comparator_51_eq,
       comparator_52_eq, comparator_53_eq, comparator_54_eq, comparator_55_eq, comparator_56_eq,
       comparator_57_eq, I_type, jal, jalr, lb, lh, Load_type, lui, lw, mul, mulh, mulhu, not_1_out,
       not_2_out, not_3_out, or_1_out, or_2_out, or_3_out, or_4_out, or_r, ori, R_type, sb, sh, sll_r, slli,
       slt, slti, sra_r, srai, srl_r, srli, Store_type, sub, sw, xor_r, xori;
  wire [5:0] InstructionSel;
  wire [15:14] rom_1_data;

  ROM #(.addrWidth(6), .dataWidth(16)) rom_1 (
    .addr(InstructionSel), .data({rom_1_data, WBSel, MemWEn, ALUSel, BSel, ASel, BrUn, ImmSel, RegWEn}));
  Priority_Encoder #(.select_enc(6)) priority_encoder_1 (
    .in0(add), .in1(mul), .in2(sub), .in3(sll_r), .in4(mulh), .in5(mulhu), .in6(slt), .in7(xor_r),
    .in8(srl_r), .in9(sra_r), .in10(or_r), .in11(and_r), .in12(lb), .in13(lh), .in14(lw), .in15(addi),
    .in16(slli), .in17(slti), .in18(xori), .in19(srli), .in20(srai), .in21(ori), .in22(andi), .in23(sb),
    .in24(sh), .in25(sw), .in26(beq), .in27(bne), .in28(blt), .in29(bge), .in30(bltu), .in31(bgeu),
    .in32(auipc), .in33(lui), .in34(jal), .in35(jalr), .out(InstructionSel));  // open: in36, in37, in38, in39, in40, in41, in42, in43, in44, in45, in46, in47, in48, in49, in50, in51, in52, in53, in54, in55, in56, in57, in58, in59, in60, in61, in62, in63, gs, en_out, en_in
  Comparator #(.mode("unsigned"), .width(3)) comparator_1 (
    .a(Instruction[14:12]), .b(3'b101), .eq(comparator_1_eq));  // open: gt, lt
  Comparator #(.mode("unsigned"), .width(7)) comparator_2 (
    .a({7{1'b0}}), .b(Instruction[31:25]), .eq(comparator_2_eq));  // open: gt, lt
  Comparator #(.mode("unsigned"), .width(3)) comparator_3 (
    .a(Instruction[14:12]), .b(3'b101), .eq(comparator_3_eq));  // open: gt, lt
  Comparator #(.mode("unsigned"), .width(7)) comparator_4 (
    .a(7'b0100000), .b(Instruction[31:25]), .eq(comparator_4_eq));  // open: gt, lt
  Comparator #(.mode("unsigned"), .width(7)) comparator_5 (
    .a(Instruction[6:0]), .b(7'b0010011), .eq(I_type));  // open: gt, lt
  Comparator #(.mode("unsigned"), .width(7)) comparator_6 (
    .a(Instruction[6:0]), .b(7'b0110011), .eq(R_type));  // open: gt, lt
  Comparator #(.mode("unsigned"), .width(7)) comparator_7 (
    .a(Instruction[6:0]), .b(7'b1100011), .eq(B_type));  // open: gt, lt
  Comparator #(.mode("unsigned"), .width(7)) comparator_8 (
    .a(Instruction[6:0]), .b(7'b0000011), .eq(Load_type));  // open: gt, lt
  Comparator #(.mode("unsigned"), .width(7)) comparator_9 (
    .a(Instruction[6:0]), .b(7'b0100011), .eq(Store_type));  // open: gt, lt
  Comparator #(.mode("unsigned"), .width(3)) comparator_10 (
    .a(Instruction[14:12]), .b(3'b000), .eq(comparator_10_eq));  // open: gt, lt
  Comparator #(.mode("unsigned"), .width(3)) comparator_11 (
    .a(Instruction[14:12]), .b(3'b111), .eq(comparator_11_eq));  // open: gt, lt
  Comparator #(.mode("unsigned"), .width(3)) comparator_12 (
    .a(Instruction[14:12]), .b(3'b111), .eq(comparator_12_eq));  // open: gt, lt
  Comparator #(.mode("unsigned"), .width(3)) comparator_13 (
    .a(Instruction[14:12]), .b(3'b110), .eq(comparator_13_eq));  // open: gt, lt
  Comparator #(.mode("unsigned"), .width(3)) comparator_14 (
    .a(Instruction[14:12]), .b(3'b100), .eq(comparator_14_eq));  // open: gt, lt
  Comparator #(.mode("unsigned"), .width(3)) comparator_15 (
    .a(Instruction[14:12]), .b(3'b001), .eq(comparator_15_eq));  // open: gt, lt
  Comparator #(.mode("unsigned"), .width(3)) comparator_16 (
    .a(Instruction[14:12]), .b(3'b010), .eq(comparator_16_eq));  // open: gt, lt
  and and_1 (addi, I_type, comparator_10_eq);
  and and_2 (andi, I_type, comparator_11_eq);
  and and_3 (andi, I_type, comparator_12_eq);
  and and_4 (ori, I_type, comparator_13_eq);
  and and_5 (xori, I_type, comparator_14_eq);
  and and_6 (slli, I_type, comparator_15_eq);
  and and_7 (srli, I_type, comparator_1_eq, comparator_2_eq);
  and and_8 (slti, I_type, comparator_16_eq);
  and and_9 (srai, I_type, comparator_3_eq, comparator_4_eq);
  not not_1 (not_1_out, BrLt);
  not not_2 (not_2_out, BrLt);
  Comparator #(.mode("unsigned"), .width(3)) comparator_17 (
    .a(Instruction[14:12]), .b(3'b000), .eq(comparator_17_eq));  // open: gt, lt
  Comparator #(.mode("unsigned"), .width(7)) comparator_18 (
    .a({7{1'b0}}), .b(Instruction[31:25]), .eq(comparator_18_eq));  // open: gt, lt
  Comparator #(.mode("unsigned"), .width(3)) comparator_19 (
    .a(Instruction[14:12]), .b(3'b000), .eq(comparator_19_eq));  // open: gt, lt
  Comparator #(.mode("unsigned"), .width(7)) comparator_20 (
    .a(7'b0100000), .b(Instruction[31:25]), .eq(comparator_20_eq));  // open: gt, lt
  Comparator #(.mode("unsigned"), .width(3)) comparator_21 (
    .a(Instruction[14:12]), .b(3'b111), .eq(comparator_21_eq));  // open: gt, lt
  Comparator #(.mode("unsigned"), .width(7)) comparator_22 (
    .a({7{1'b0}}), .b(Instruction[31:25]), .eq(comparator_22_eq));  // open: gt, lt
  Comparator #(.mode("unsigned"), .width(3)) comparator_23 (
    .a(Instruction[14:12]), .b(3'b110), .eq(comparator_23_eq));  // open: gt, lt
  Comparator #(.mode("unsigned"), .width(7)) comparator_24 (
    .a({7{1'b0}}), .b(Instruction[31:25]), .eq(comparator_24_eq));  // open: gt, lt
  Comparator #(.mode("unsigned"), .width(3)) comparator_25 (
    .a(Instruction[14:12]), .b(3'b100), .eq(comparator_25_eq));  // open: gt, lt
  Comparator #(.mode("unsigned"), .width(7)) comparator_26 (
    .a({7{1'b0}}), .b(Instruction[31:25]), .eq(comparator_26_eq));  // open: gt, lt
  Comparator #(.mode("unsigned"), .width(3)) comparator_27 (
    .a(Instruction[14:12]), .b(3'b001), .eq(comparator_27_eq));  // open: gt, lt
  Comparator #(.mode("unsigned"), .width(7)) comparator_28 (
    .a({7{1'b0}}), .b(Instruction[31:25]), .eq(comparator_28_eq));  // open: gt, lt
  Comparator #(.mode("unsigned"), .width(3)) comparator_29 (
    .a(Instruction[14:12]), .b(3'b101), .eq(comparator_29_eq));  // open: gt, lt
  Comparator #(.mode("unsigned"), .width(7)) comparator_30 (
    .a({7{1'b0}}), .b(Instruction[31:25]), .eq(comparator_30_eq));  // open: gt, lt
  Comparator #(.mode("unsigned"), .width(3)) comparator_31 (
    .a(Instruction[14:12]), .b(3'b101), .eq(comparator_31_eq));  // open: gt, lt
  Comparator #(.mode("unsigned"), .width(7)) comparator_32 (
    .a(7'b0100000), .b(Instruction[31:25]), .eq(comparator_32_eq));  // open: gt, lt
  Comparator #(.mode("unsigned"), .width(3)) comparator_33 (
    .a(Instruction[14:12]), .b(3'b010), .eq(comparator_33_eq));  // open: gt, lt
  Comparator #(.mode("unsigned"), .width(7)) comparator_34 (
    .a({7{1'b0}}), .b(Instruction[31:25]), .eq(comparator_34_eq));  // open: gt, lt
  Comparator #(.mode("unsigned"), .width(3)) comparator_35 (
    .a(Instruction[14:12]), .b(3'b000), .eq(comparator_35_eq));  // open: gt, lt
  Comparator #(.mode("unsigned"), .width(7)) comparator_36 (
    .a(7'b0000001), .b(Instruction[31:25]), .eq(comparator_36_eq));  // open: gt, lt
  Comparator #(.mode("unsigned"), .width(3)) comparator_37 (
    .a(Instruction[14:12]), .b(3'b001), .eq(comparator_37_eq));  // open: gt, lt
  Comparator #(.mode("unsigned"), .width(7)) comparator_38 (
    .a(7'b0000001), .b(Instruction[31:25]), .eq(comparator_38_eq));  // open: gt, lt
  Comparator #(.mode("unsigned"), .width(3)) comparator_39 (
    .a(Instruction[14:12]), .b(3'b011), .eq(comparator_39_eq));  // open: gt, lt
  Comparator #(.mode("unsigned"), .width(7)) comparator_40 (
    .a(7'b0000001), .b(Instruction[31:25]), .eq(comparator_40_eq));  // open: gt, lt
  or or_1 (or_1_out, BrEq, not_1_out);
  or or_2 (or_2_out, BrEq, not_2_out);
  not not_3 (not_3_out, BrEq);
  and and_10 (and_10_out, beq, BrEq);
  and and_11 (and_11_out, bge, or_1_out);
  and and_12 (and_12_out, bgeu, or_2_out);
  and and_13 (and_13_out, blt, BrLt);
  and and_14 (and_14_out, bltu, BrLt);
  and and_15 (and_15_out, bne, not_3_out);
  and and_16 (add, R_type, comparator_17_eq, comparator_18_eq);
  and and_17 (sub, R_type, comparator_19_eq, comparator_20_eq);
  and and_18 (and_r, R_type, comparator_21_eq, comparator_22_eq);
  and and_19 (or_r, R_type, comparator_23_eq, comparator_24_eq);
  and and_20 (xor_r, R_type, comparator_25_eq, comparator_26_eq);
  and and_21 (sll_r, R_type, comparator_27_eq, comparator_28_eq);
  and and_22 (srl_r, R_type, comparator_29_eq, comparator_30_eq);
  and and_23 (sra_r, R_type, comparator_31_eq, comparator_32_eq);
  and and_24 (slt, R_type, comparator_33_eq, comparator_34_eq);
  and and_25 (mul, R_type, comparator_35_eq, comparator_36_eq);
  and and_26 (mulh, R_type, comparator_37_eq, comparator_38_eq);
  and and_27 (mulhu, R_type, comparator_39_eq, comparator_40_eq);
  or or_3 (or_3_out, and_10_out, and_11_out, and_12_out, and_13_out, and_14_out, and_15_out);
  or or_4 (or_4_out, jal, jalr);
  Comparator #(.mode("unsigned"), .width(3)) comparator_41 (
    .a(Instruction[14:12]), .b(3'b000), .eq(comparator_41_eq));  // open: gt, lt
  Comparator #(.mode("unsigned"), .width(3)) comparator_42 (
    .a(Instruction[14:12]), .b(3'b101), .eq(comparator_42_eq));  // open: gt, lt
  Comparator #(.mode("unsigned"), .width(3)) comparator_43 (
    .a(Instruction[14:12]), .b(3'b111), .eq(comparator_43_eq));  // open: gt, lt
  Comparator #(.mode("unsigned"), .width(3)) comparator_44 (
    .a(Instruction[14:12]), .b(3'b100), .eq(comparator_44_eq));  // open: gt, lt
  Comparator #(.mode("unsigned"), .width(3)) comparator_45 (
    .a(Instruction[14:12]), .b(3'b110), .eq(comparator_45_eq));  // open: gt, lt
  Comparator #(.mode("unsigned"), .width(3)) comparator_46 (
    .a(Instruction[14:12]), .b(3'b001), .eq(comparator_46_eq));  // open: gt, lt
  or or_5 (BrUn, bgeu, bltu);
  or or_6 (PCSel, or_3_out, or_4_out);
  and and_28 (beq, B_type, comparator_41_eq);
  and and_29 (bge, B_type, comparator_42_eq);
  and and_30 (bgeu, B_type, comparator_43_eq);
  and and_31 (blt, B_type, comparator_44_eq);
  and and_32 (bltu, B_type, comparator_45_eq);
  and and_33 (bne, B_type, comparator_46_eq);
  Comparator #(.mode("unsigned"), .width(7)) comparator_47 (
    .a(Instruction[6:0]), .b(7'b0010111), .eq(auipc));  // open: gt, lt
  Comparator #(.mode("unsigned"), .width(7)) comparator_48 (
    .a(Instruction[6:0]), .b(7'b0110111), .eq(lui));  // open: gt, lt
  Comparator #(.mode("unsigned"), .width(7)) comparator_49 (
    .a(Instruction[6:0]), .b(7'b1101111), .eq(jal));  // open: gt, lt
  Comparator #(.mode("unsigned"), .width(7)) comparator_50 (
    .a(Instruction[6:0]), .b(7'b1100111), .eq(comparator_50_eq));  // open: gt, lt
  Comparator #(.mode("unsigned"), .width(3)) comparator_51 (
    .a(Instruction[14:12]), .b(3'b000), .eq(comparator_51_eq));  // open: gt, lt
  Comparator #(.mode("unsigned"), .width(3)) comparator_52 (
    .a(Instruction[14:12]), .b(3'b000), .eq(comparator_52_eq));  // open: gt, lt
  Comparator #(.mode("unsigned"), .width(3)) comparator_53 (
    .a(Instruction[14:12]), .b(3'b001), .eq(comparator_53_eq));  // open: gt, lt
  Comparator #(.mode("unsigned"), .width(3)) comparator_54 (
    .a(Instruction[14:12]), .b(3'b010), .eq(comparator_54_eq));  // open: gt, lt
  Comparator #(.mode("unsigned"), .width(3)) comparator_55 (
    .a(Instruction[14:12]), .b(3'b000), .eq(comparator_55_eq));  // open: gt, lt
  Comparator #(.mode("unsigned"), .width(3)) comparator_56 (
    .a(Instruction[14:12]), .b(3'b001), .eq(comparator_56_eq));  // open: gt, lt
  Comparator #(.mode("unsigned"), .width(3)) comparator_57 (
    .a(Instruction[14:12]), .b(3'b010), .eq(comparator_57_eq));  // open: gt, lt
  and and_34 (lb, Load_type, comparator_52_eq);
  and and_35 (lh, Load_type, comparator_53_eq);
  and and_36 (lw, Load_type, comparator_54_eq);
  and and_37 (sb, Store_type, comparator_55_eq);
  and and_38 (sh, Store_type, comparator_56_eq);
  and and_39 (sw, Store_type, comparator_57_eq);
  and and_40 (jalr, comparator_50_eq, comparator_51_eq);

  // Other names for the same wires on the sheet: Opcode[6:0] = Instruction[6:0]; Funct3[2:0] = Instruction[14:12];
  //   Funct7[6:0] = Instruction[31:25]

  // Notes on the sheet:
  //   INPUTS to your circuit
  //   contents of rom_1 (hex, n*v repeats v):
  //   1001 1401 1601 1081 1481 1581 1101 1201 1281 1681 1301 1381 841 841 841 1041 10c1 1141 1241 12c1
  //   16c1 1341 13c1 842 842 842 4*64 74 74 1067 17c7 2069 2041
  //   ROM FOR CONTROL LOGIC
  //   DON'T CHANGE THE LOCATIONS OF THE INPUTS AND OUTPUTS!
  //   This is only if you choose to do the ROM option
  //   OUTPUT from your circuit
endmodule
