// Logisim project cpu.circ as structural Verilog: 1 circuit, main circuit cpu
module cpu (
  input  clk,
  input  [31:0] Instruction,
  input  [31:0] MemReadData,
  output [31:0] MemAddress,
  output [31:0] ProgramCounter,
  output [31:0] ra,
  output [31:0] sp,
  output [31:0] t0,
  output [31:0] t1,
  output [31:0] t2,
  output [31:0] s0,
  output [31:0] s1,
  output [31:0] a0,
  output [3:0] MemWriteMask,
  output [31:0] MemWriteData
);

  wire ASel, BrEq, BrLt, BrUn, BSel, MemWEn, PCSel, regfile_1_p7, regfile_1_p8, regfile_1_p20, regfile_1_p22,
       regfile_1_p24, RegWEn;
  wire [1:0] WBSel;
  wire [2:0] ImmSel;
  wire [3:0] ALUSel;
  wire [31:0] adder_1_out, DataToReg, immediate, Instruction_stage2, multiplexer_1_out, multiplexer_2_out,
       multiplexer_3_out, multiplexer_4_out, PC_add4, ProgramCounter_stage2, ReadData1, ReadData2, WB;

  Register #(.width(32)) register_1 (.D(multiplexer_1_out), .clk(clk), .Q(Instruction_stage2));  // open: en, clr
  Multiplexer #(.width(32)) multiplexer_1 (.in0(Instruction), .in1(32'h13), .out(multiplexer_1_out), .sel(PCSel));
  branch_comp branch_comp_1 (.BrData1(ReadData1), .BrData2(ReadData2), .BrUn(BrUn), .BrEq(BrEq), .BrLt(BrLt));
  imm_gen imm_gen_1 (.Instruction(Instruction_stage2), .ImmSel(ImmSel), .Immediate(immediate));
  Adder #(.width(32)) adder_1 (.a(ProgramCounter), .b(32'h4), .out(adder_1_out));  // open: cin, cout
  Multiplexer #(.width(32)) multiplexer_2 (.in0(adder_1_out), .in1(MemAddress), .out(multiplexer_2_out), .sel(PCSel));
  Register #(.width(32)) PC (.D(multiplexer_2_out), .clk(clk), .Q(ProgramCounter));  // open: en, clr
  control_logic control_logic_1 (
    .Instruction(Instruction_stage2), .BrEq(BrEq), .BrLt(BrLt), .PCSel(PCSel), .RegWEn(RegWEn),
    .ImmSel(ImmSel), .BrUn(BrUn), .ASel(ASel), .BSel(BSel), .ALUSel(ALUSel), .MemWEn(MemWEn), .WBSel(WBSel));
  // regfile regfile_1: pin names not known; wires that end beside it: Instruction_stage2[19:15], Instruction_stage2[24:20], Instruction_stage2[11:7], WB, RegWEn, clk, regfile_1_p7, regfile_1_p8, regfile_1_p8, ra, sp, t0, t1, t2, s0, s1, a0, ReadData1, ReadData2, regfile_1_p20, regfile_1_p20, regfile_1_p22, regfile_1_p22, regfile_1_p24, regfile_1_p24
  Register #(.width(32)) register_2 (.D(ProgramCounter), .clk(clk), .Q(ProgramCounter_stage2));  // open: en, clr
  Adder #(.width(32)) adder_2 (.a(ProgramCounter_stage2), .b(32'h4), .out(PC_add4));  // open: cin, cout
  Multiplexer #(.width(32)) multiplexer_3 (
    .in0(ReadData1), .in1(ProgramCounter_stage2), .out(multiplexer_3_out), .sel(ASel));
  Multiplexer #(.width(32)) multiplexer_4 (.in0(ReadData2), .in1(immediate), .out(multiplexer_4_out), .sel(BSel));
  alu alu_1 (.A(multiplexer_3_out), .B(multiplexer_4_out), .ALUSel(ALUSel), .ALUResult(MemAddress));
  Multiplexer #(.select(2), .width(32)) multiplexer_5 (
    .in0(DataToReg), .in1(MemAddress), .in2(PC_add4), .out(WB), .sel(WBSel));  // open: in3
  partial_store partial_store_1 (
    .Instruction(Instruction_stage2), .MemAddress(MemAddress), .DataFromReg(ReadData2), .MemWEn(MemWEn),
    .MemWriteMask(MemWriteMask), .DataToMem(MemWriteData));
  partial_load partial_load_1 (
    .Instruction(Instruction_stage2), .MemAddress(MemAddress), .DataFromMem(MemReadData),
    .DataToReg(DataToReg));

  // Other names for the same wires on the sheet: ALUResult[31:0] = MemAddress; rd[4:0] = Instruction_stage2[11:7];
  //   rs1[4:0] = Instruction_stage2[19:15]; rs2[4:0] = Instruction_stage2[24:20]

  // Notes on the sheet:
  //   To IMEM
  //   IMEM (do **NOT** move this)
  //   From IMEM
  //   Inputs/Outputs for testing. Do **NOT** move these.
  //   To DMEM
  //   DMEM (do **NOT** move this)
  //   From DMEM
endmodule
