// Logisim project imm-gen.circ as structural Verilog: 1 circuit, main circuit imm_gen
module imm_gen (
  input  [31:0] Instruction,
  input  [2:0] ImmSel,
  output [31:0] Immediate
);

  wire [31:11] I_Imm, S_Imm;
  wire [31:12] B_Imm;
  wire [31:20] J_Imm;

  Multiplexer #(.width(21)) multiplexer_1 (.in0({21{1'b0}}), .in1({21{1'b1}}), .out(I_Imm), .sel(Instruction[31]));
  Multiplexer #(.width(21)) multiplexer_2 (.in0({21{1'b0}}), .in1({21{1'b1}}), .out(S_Imm), .sel(Instruction[31]));
  Multiplexer #(.width(20)) multiplexer_3 (.in0({20{1'b0}}), .in1({20{1'b1}}), .out(B_Imm), .sel(Instruction[31]));
  Multiplexer #(.width(12)) multiplexer_4 (.in0({12{1'b0}}), .in1({12{1'b1}}), .out(J_Imm), .sel(Instruction[31]));
  Multiplexer #(.select(3), .width(32)) multiplexer_5 (
    .in0({I_Imm, Instruction[30:20]}), .in1({S_Imm, Instruction[30:25], Instruction[11:7]}),
    .in2({B_Imm, Instruction[7], Instruction[30:25], Instruction[11:8], 1'b0}),
    .in3({Instruction[31:12], {12{1'b0}}}),
    .in4({J_Imm, Instruction[19:12], Instruction[20], Instruction[30:21], 1'b0}), .out(Immediate),
    .sel(ImmSel));  // open: in5, in6, in7

  // Other names for the same wires on the sheet: B_Imm[11:1] = {Instruction[7], Instruction[30:25], Instruction[11:8]};
  //   S_Imm[10:0] = {Instruction[30:25], Instruction[11:7]}; I_Imm[10:0] = Instruction[30:20];
  //   J_Imm[19:1] = {Instruction[19:12], Instruction[20], Instruction[30:21]}; U_Imm[31:12] = Instruction[31:12];
  //   sel = Instruction[31]

  // Notes on the sheet:
  //   INPUTS to your circuit
  //   DON'T CHANGE THE LOCATIONS OF THE INPUTS AND OUTPUTS!
  //   OUTPUT from your circuit
endmodule
