// Logisim project part_a_cpu.circ as structural Verilog: 1 circuit, main circuit cpu
module cpu (
  input  clk,
  input  [31:0] Instruction,
  input  [31:0] MemReadData,
  output [31:0] MemAddress,
  output [31:0] ProgramCounter,
  output [31:0] ra,
  output [31:0] sp,
  output [31:0] t0,
  output [31:0] t1,
  output [31:0] t2,
  output [31:0] s0,
  output [31:0] s1,
  output [31:0] a0,
  output [3:0] MemWriteMask,
  output [31:0] MemWriteData
);

  wire regfile_1_p6, regfile_1_p7, regfile_1_p18, regfile_1_p20, regfile_1_p22;
  wire [31:0] adder_1_out, imm_gen_1_immediate, ReadData1, WB;

  Adder #(.width(32)) adder_1 (.a(ProgramCounter), .b(32'h4), .out(adder_1_out));  // open: cin, cout
  Register #(.width(32)) PC (.D(adder_1_out), .clk(clk), .Q(ProgramCounter));  // open: en, clr
  // regfile regfile_1: pin names not known; wires that end beside it: Instruction[11:7], WB, 1'b1, clk, Instruction[19:15], regfile_1_p6, regfile_1_p7, regfile_1_p7, ra, sp, t0, t1, t2, s0, s1, a0, ReadData1, regfile_1_p18, regfile_1_p18, regfile_1_p20, regfile_1_p20, regfile_1_p22
  // control_logic control_logic_1: pin names not known
  imm_gen imm_gen_1 (.Instruction(Instruction), .Immediate(imm_gen_1_immediate));  // open: ImmSel
  alu alu_1 (.A(ReadData1), .B(imm_gen_1_immediate), .ALUSel(4'b0000), .ALUResult(WB));
  // branch_comp branch_comp_1: pin names not known
  // partial_store partial_store_1: pin names not known
  // partial_load partial_load_1: pin names not known

  // Other names for the same wires on the sheet: rd[4:0] = Instruction[11:7]; rs1[4:0] = Instruction[19:15]

  // Notes on the sheet:
  //   To IMEM
  //   IMEM (do **NOT** move this)
  //   From IMEM
  //   Inputs/Outputs for testing. Do **NOT** move these.
  //   To DMEM
  //   DMEM (do **NOT** move this)
  //   From DMEM
endmodule
